// Digital circuit TBOS Testing.dig as structural Verilog
module TBOS_Testing (
  input  clk,
  input  Manual
);

  wire and_1_out, button_1_out, button_2_out, button_3_out, button_4_out, delay_1_out, multiplexer_1_out,
       Resume_Proc_out, telescope_computing_system_1_running;
  wire [15:0] Root_Drive_d, TBOS_2_3_d, telescope_computing_system_1_os_adr,
       telescope_computing_system_1_status_code;
  wire [17:17] rs_ff_as_1_q;
  wire [18:0] telescope_computing_system_1_gpo_1, telescope_computing_system_1_tk1_out;
  wire [33:0] telescope_computing_system_1_d0_out;

  LED OS_Is_Running (.in(telescope_computing_system_1_running));
  // Probe Status on telescope_computing_system_1_status_code
  Button button_1 (.out(button_1_out));
  Multiplexer multiplexer_1 (.sel(Manual), .in_0(clk), .in_1(button_2_out), .out(multiplexer_1_out));
  Button button_2 (.out(button_2_out));
  Telescope_Computing_System telescope_computing_system_1 (
    .Running(telescope_computing_system_1_running), .Status_Code(telescope_computing_system_1_status_code),
    .Power_On(button_1_out), .Clock_Input(multiplexer_1_out), .Pause_CPU(button_3_out), .PAUS(1'b0),
    .STOP(button_4_out), .OS_Adr(telescope_computing_system_1_os_adr), .OS_In(TBOS_2_3_d),
    .D0_In(Root_Drive_d), .D0_Out(telescope_computing_system_1_d0_out), .D1_In({16{1'b0}}),
    .D2_In({16{1'b0}}), .D3_In({16{1'b0}}), .TNET_I_0({20{1'b0}}), .TNET_I_1({20{1'b0}}),
    .TNET_I_2({20{1'b0}}), .TNET_I_3({20{1'b0}}), .K0_In({17{1'b0}}),
    .TK1_Out(telescope_computing_system_1_tk1_out), .K1_In({17{1'b0}}), .K2_In({17{1'b0}}),
    .K3_In({17{1'b0}}), .GPI_0({18{1'b0}}), .GPO_1(telescope_computing_system_1_gpo_1),
    .GPI_1({rs_ff_as_1_q[17], {17{1'b0}}}), .GPI_2({18{1'b0}}), .GPI_3({18{1'b0}}));  // open: D1_Out, D2_Out, D3_Out, TNET_O_0, TNET_O_1, TNET_O_2, TNET_O_3, TK0_Out, TK2_Out, TK3_Out, GPO_0, GPO_2, GPO_3
  Button button_3 (.out(button_3_out));
  Button button_4 (.out(button_4_out));
  Button Resume_Proc (.out(Resume_Proc_out));
  Delay delay_1 (.in(Resume_Proc_out), .out(delay_1_out));
  and and_1 (and_1_out, Resume_Proc_out, ~delay_1_out);  // And
  RS_FF_AS rs_ff_as_1 (.S(and_1_out), .R(telescope_computing_system_1_gpo_1[17]), .Q(rs_ff_as_1_q[17]));  // open: nQ
  // Probe OS Boot Address on telescope_computing_system_1_os_adr
  ROM #(.AddrBits(16), .Bits(16)) TBOS_2_3 (.A(telescope_computing_system_1_os_adr), .sel(1'b1), .D(TBOS_2_3_d));
  Terminal terminal_1 (
    .D(telescope_computing_system_1_tk1_out[15:0]), .C(telescope_computing_system_1_tk1_out[18]),
    .en(telescope_computing_system_1_tk1_out[17]));
  EEPROMDualPort #(.AddrBits(16), .Bits(16)) Root_Drive (
    .A(telescope_computing_system_1_d0_out[15:0]), .Din(telescope_computing_system_1_d0_out[31:16]),
    .str(telescope_computing_system_1_d0_out[32]), .C(telescope_computing_system_1_d0_out[33]), .ld(1'b1),
    .D(Root_Drive_d));

  // Notes on the sheet:
  //   clk: Hz: 2000
  //   contents of TBOS_2_3 (hex, n*v repeats v):
  //   7df,4600,26e,520*0,32*1,66*0,a630,a730,50a0,f000,5090,1,50a0,e000
  //   ,3090,5010,7df,5000,400,ae10,b912,5000,40,bb01,3078,b974,4600
  //   ,3be,50a0,0,3078,b974,4600,5f3,d961,4a00,28f,5000,ff00,4600,29f
  //   ,3006,50a0,4,3078,b974,4600,3e2,50a0,f000,5090,2,b000,7000,64
  //   ,4600,2a8,50a0,e800,3090,50a0,f000,3090,0,4600,2a5,b100,6000,62
  //   ,9200,4000,316,b100,6000,64,3060,b110,6011,63,b911,b150,af61,b901
  //   ,af01,cb06,4000,308,6020,66,d620,4a00,2b8,d622,4a00,2e3,d624,4a00
  //   ,2b8,6030,42,9931,4a00,2b8,b130,6033,65,60a3,8,d625,4200,2d9,4c00
  //   ,2b8,4600,2db,4d00,2b8,3040,6000,22,3078,b974,4600,57e,3004,7000
  //   ,64,bd0c,5010,86,a901,7000,65,60e0,a,50f0,31a,50d0,200,60c0,b
  //   ,60a0,8,60b0,9,6070,7,6060,6,6050,5,6040,4,6030,3,6020,2,6010
  //   ,1,6000,0,1000,b951,db54,4800,2bd,b100,6000,26b,9200,4800,6a6
  //   ,5000,dead,4600,29f,5000,600d,4600,29f,7000,362,b100,6000,65,7010
  //   ,1,b110,6011,362,7010,0,7020,2,7030,3,7040,4,7050,5,7060,6,7070
  //   ,7,70b0,9,70e0,a,70a0,8,b1b0,5000,700,a10a,b508,db04,4000,2a8
  //   ,db05,4000,6b8,db06,4000,66e,db07,4000,66e,db01,4000,49b,db03
  //   ,4000,4a2,db00,4000,4ae,db02,4800,35e,b100,6000,65,5010,ff03,7010
  //   ,6,4600,2a8,5000,ff01,4600,29f,0,b100,6000,64,6000,66,d602,4200
  //   ,2a8,b100,6000,65,60b0,9,60a0,8,6070,7,6060,6,6050,5,6040,4,6030
  //   ,3,6020,2,6010,1,6000,0,1000,9210,4000,38c,7090,0,b901,9b11,4800
  //   ,386,3087,bbb1,704b,0,3040,5000,40,b110,b120,6032,206,cb10,4900
  //   ,3b9,3061,b911,d514,4200,3a3,b921,b722,6032,206,c636,4200,397
  //   ,3004,9b01,4000,3ba,b911,d514,4200,3b2,b921,b722,6032,206,c631
  //   ,4a00,3a7,5000,40,4600,397,b060,604b,0,b9b1,3087,b120,6022,26c
  //   ,4600,3c8,b120,6022,26d,4600,3c8,7022,3d2,a910,3020,b524,6032
  //   ,206,cb01,4000,3df,f000,b901,d504,4200,3cf,7032,206,b921,b722
  //   ,6032,206,4600,3cf,7032,206,3087,bbb1,704b,0,304a,b010,b911,6021
  //   ,2,d62f,4200,3e7,b130,b120,b62f,7021,2,7031,22,7031,42,6023,62
  //   ,b921,7022,62,6023,63,cb12,4100,402,7011,63,5020,1,7021,66,3021
  //   ,bd2c,5030,86,a923,b130,7032,0,7032,1,7032,2,7032,3,7032,4,7032
  //   ,5,7032,6,7032,7,7032,a,7032,9,3034,7032,8,7002,b,3001,3060,3047
  //   ,3078,b974,4600,431,3074,604b,0,b9b1,3087,9200,4000,461,6010,2
  //   ,5020,3e0,a022,a112,5020,7c00,a022,a112,b120,6022,64,3032,b43a
  //   ,a213,7010,2,6032,2,5010,1f,8113,4800,452,a230,7032,2,4600,461
  //   ,6021,2,5030,3e0,8132,4000,45d,b535,3013,4600,452,b405,a220,7021
  //   ,2,3087,bbb1,704b,0,9200,4000,497,6010,2,5020,7c00,a121,b52a,6032
  //   ,2,5040,1f,a143,cb40,4800,483,5040,1f,a044,a134,5040,3e0,a141
  //   ,b545,a234,7032,2,4600,497,6024,2,5030,3e0,a132,b535,cb30,4000
  //   ,48f,3043,4600,483,5030,3e0,a113,a033,a123,a221,7024,2,604b,0
  //   ,b9b1,3087,50a0,f000,5090,1111,0,4600,363,50a0,f000,5090,2222
  //   ,0,b100,3078,b974,4600,4b9,4600,2a8,5000,26a,3078,b974,4600,5ae
  //   ,50a0,f800,b190,4600,363,bbb1,707b,0,b110,3078,b974,4600,4d5,b100
  //   ,6000,63,9200,4000,4cf,6010,66,d610,4200,4cf,bb01,4600,4c4,7000
  //   ,63,607b,0,b9b1,3087,bbb2,704b,0,707b,1,3040,9210,4000,4ea,6020
  //   ,2,5000,3e0,8102,4000,4ee,b505,5070,4ee,4600,4d5,3078,b974,4600
  //   ,462,6014,66,d612,4a00,51b,d613,4a00,4fc,b110,6011,26b,bb11,7011
  //   ,26b,6014,22,6021,0,b921,7021,0,b000,b120,6022,63,b921,b901,cb02
  //   ,4000,51b,6030,22,cb31,4800,508,6030,42,cb31,4900,508,b931,7030
  //   ,42,4600,508,b110,7014,22,7014,42,6014,66,d611,4200,537,3024,bd2c
  //   ,b92b,6022,86,3012,5030,400,ae13,5000,ff,a102,b408,ae03,3078,b974
  //   ,4600,3c3,6024,2,5030,1f,8123,4000,544,3002,b010,3078,b974,4600
  //   ,4d5,b100,7004,2,b100,6000,62,bb01,7000,62,b100,7004,66,604b,0
  //   ,607b,1,b9b2,3087,6020,0,bb21,7020,0,9220,4900,57c,7001,22,7021
  //   ,42,6031,66,b632,5020,22a,cb02,4100,576,5020,26b,cb02,4900,576
  //   ,b120,6022,26b,b921,7022,26b,b633,7031,66,5060,1,4600,57d,b160
  //   ,3087,6010,0,b911,7010,0,b010,b120,6022,63,b921,b911,cb12,4000
  //   ,5ad,6031,22,cb30,4800,588,6031,42,b931,7031,42,9230,4800,588
  //   ,7031,22,6031,66,b732,b734,d633,4a00,5a9,b160,6066,26b,bb61,7066
  //   ,26b,b733,7031,66,4600,588,3087,b010,b120,b911,5030,20,cb13,4000
  //   ,5d3,6031,22,cb30,4800,5b0,6061,66,b762,b764,d663,4a00,5c9,b130
  //   ,6033,26b,bb31,7033,26b,b763,7061,66,b130,7031,22,7031,42,b921
  //   ,4600,5b0,6010,0,a912,7010,0,3087,bbb3,707b,0,bd02,b110,b6ad,3091
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  //   Currently configured to run: I/O Waiting Test
  //   contents of Root_Drive (hex, n*v repeats v):
  //   92,4600,5,0,0,0,5000,1,5020,82,b130,5010,31,2000,5010,48,2000
  //   ,5010,66,2000,5000,4,5010,2,2000,50a0,4800,5090,a,5090,41,5090
  //   ,6c,5090,6c,5090,20,5090,64,5090,6f,5090,6e,5090,65,5090,21,5000
  //   ,2,2000,5020,5,5010,3,5030,9,50a0,6800,5000,3,2000,3002,2000,3003
  //   ,2000,b190,50a0,4800,5090,41,5000,2,2000,5020,4,5010,3,5030,9
  //   ,50a0,6800,5040,5,5050,4,5000,3,2000,3002,2000,3004,3015,2000
  //   ,3003,2000,b190,50a0,4800,5090,42,5000,2,2000,5020,4,5010,4,5030
  //   ,9,50a0,6800,5000,3,2000,3002,2000,3003,2000,b190,50a0,4800,5090
  //   ,43,5000,5,5010,2,2000,5000,2,2000
endmodule
